// Logisim project KoggeStone.circ as structural Verilog: 6 circuits, main circuit KoggeStone
module KoggeStone (
  input  [31:0] A,
  input  [31:0] B,
  input  Subtraction,
  output [31:0] Result,
  output Carry
);

  wire black_01_1_out_5, black_01_1_out_6, black_01_1_out_7, black_01_1_out_8, black_01_2_out_5,
       black_01_2_out_6, black_01_2_out_7, black_01_2_out_8, black_01_3_out_5, black_01_3_out_6,
       black_01_3_out_7, black_01_3_out_8, black_01_4_out_5, black_01_4_out_6, black_01_4_out_7,
       black_01_4_out_8, black_01_5_out_5, black_01_5_out_6, black_01_5_out_7, black_01_5_out_8,
       black_01_6_out_5, black_01_6_out_6, black_01_6_out_7, black_01_6_out_8, black_01_7_out_5,
       black_01_7_out_6, black_01_7_out_7, black_01_7_out_8, black_01_8_out_5, black_01_8_out_6,
       black_01_8_out_7, black_01_8_out_8, black_01_9_out_5, black_01_9_out_6, black_01_9_out_7,
       black_01_9_out_8, black_01_10_out_5, black_01_10_out_6, black_01_10_out_7, black_01_10_out_8,
       black_01_11_out_5, black_01_11_out_6, black_01_11_out_7, black_01_11_out_8, black_01_12_out_5,
       black_01_12_out_6, black_01_12_out_7, black_01_12_out_8, black_01_13_out_5, black_01_13_out_6,
       black_01_13_out_7, black_01_13_out_8, black_01_14_out_5, black_01_14_out_6, black_01_14_out_7,
       black_01_14_out_8, black_01_15_out_5, black_01_15_out_6, black_01_15_out_7, black_01_15_out_8,
       black_01_16_out_5, black_01_16_out_6, black_01_16_out_7, black_01_16_out_8, black_01_17_out_5,
       black_01_17_out_6, black_01_17_out_7, black_01_17_out_8, black_01_18_out_5, black_01_18_out_6,
       black_01_18_out_7, black_01_18_out_8, black_01_19_out_5, black_01_19_out_6, black_01_19_out_7,
       black_01_19_out_8, black_01_20_out_5, black_01_20_out_6, black_01_20_out_7, black_01_20_out_8,
       black_01_21_out_5, black_01_21_out_6, black_01_21_out_7, black_01_21_out_8, black_01_22_out_5,
       black_01_22_out_6, black_01_22_out_7, black_01_22_out_8, black_01_23_out_5, black_01_23_out_6,
       black_01_23_out_7, black_01_23_out_8, black_01_24_out_5, black_01_24_out_6, black_01_24_out_7,
       black_01_24_out_8, black_01_25_out_5, black_01_25_out_6, black_01_25_out_7, black_01_25_out_8,
       black_01_26_out_5, black_01_26_out_6, black_01_26_out_7, black_01_26_out_8, black_01_27_out_5,
       black_01_27_out_6, black_01_27_out_7, black_01_27_out_8, black_01_28_out_5, black_01_28_out_6,
       black_01_28_out_7, black_01_28_out_8, black_01_29_out_5, black_01_29_out_6, black_01_29_out_7,
       black_01_29_out_8, black_01_30_out_5, black_01_30_out_6, black_01_30_out_7, black_01_30_out_8,
       black_01_31_out_5, black_01_31_out_6, black_01_31_out_7, black_01_31_out_8, black_01_32_out_5,
       black_01_32_out_6, black_01_32_out_7, black_01_32_out_8, black_01_33_out_5, black_01_33_out_6,
       black_01_33_out_7, black_01_33_out_8, black_01_34_out_5, black_01_34_out_6, black_01_34_out_7,
       black_01_34_out_8, black_01_35_out_5, black_01_35_out_6, black_01_35_out_7, black_01_35_out_8,
       black_01_36_out_5, black_01_36_out_6, black_01_36_out_7, black_01_36_out_8, black_01_37_out_5,
       black_01_37_out_6, black_01_37_out_7, black_01_37_out_8, black_01_38_out_5, black_01_38_out_6,
       black_01_38_out_7, black_01_38_out_8, black_01_39_out_5, black_01_39_out_6, black_01_39_out_7,
       black_01_39_out_8, black_01_40_out_5, black_01_40_out_6, black_01_40_out_7, black_01_40_out_8,
       black_01_41_out_5, black_01_41_out_6, black_01_41_out_7, black_01_41_out_8, black_01_42_out_5,
       black_01_42_out_6, black_01_42_out_7, black_01_42_out_8, black_01_43_out_5, black_01_43_out_6,
       black_01_43_out_7, black_01_43_out_8, black_01_44_out_5, black_01_44_out_6, black_01_44_out_7,
       black_01_44_out_8, black_01_45_out_5, black_01_45_out_6, black_01_45_out_7, black_01_45_out_8,
       black_01_46_out_5, black_01_46_out_6, black_01_46_out_7, black_01_46_out_8, black_01_47_out_5,
       black_01_47_out_6, black_01_47_out_7, black_01_47_out_8, black_01_48_out_5, black_01_48_out_6,
       black_01_48_out_7, black_01_48_out_8, black_01_49_out_5, black_01_49_out_6, black_01_49_out_7,
       black_01_49_out_8, black_01_50_out_5, black_01_50_out_6, black_01_50_out_7, black_01_50_out_8,
       black_01_51_out_5, black_01_51_out_6, black_01_51_out_7, black_01_51_out_8, black_01_52_out_5,
       black_01_52_out_6, black_01_52_out_7, black_01_52_out_8, black_01_53_out_5, black_01_53_out_6,
       black_01_53_out_7, black_01_53_out_8, black_01_54_out_5, black_01_54_out_6, black_01_54_out_7,
       black_01_54_out_8, black_01_55_out_5, black_01_55_out_6, black_01_55_out_7, black_01_55_out_8,
       black_01_56_out_5, black_01_56_out_6, black_01_56_out_7, black_01_56_out_8, black_01_57_out_5,
       black_01_57_out_6, black_01_57_out_7, black_01_57_out_8, black_01_58_out_5, black_01_58_out_6,
       black_01_58_out_7, black_01_58_out_8, black_01_59_out_5, black_01_59_out_6, black_01_59_out_7,
       black_01_59_out_8, black_01_60_out_5, black_01_60_out_6, black_01_60_out_7, black_01_60_out_8,
       black_01_61_out_5, black_01_61_out_6, black_01_61_out_7, black_01_61_out_8, black_01_62_out_5,
       black_01_62_out_6, black_01_62_out_7, black_01_62_out_8, black_01_63_out_5, black_01_63_out_6,
       black_01_63_out_7, black_01_63_out_8, black_01_64_out_5, black_01_64_out_6, black_01_64_out_7,
       black_01_64_out_8, black_01_65_out_5, black_01_65_out_6, black_01_65_out_7, black_01_65_out_8,
       black_01_66_out_5, black_01_66_out_6, black_01_66_out_7, black_01_66_out_8, black_01_67_out_5,
       black_01_67_out_6, black_01_67_out_7, black_01_67_out_8, black_01_68_out_5, black_01_68_out_6,
       black_01_68_out_7, black_01_68_out_8, black_01_69_out_5, black_01_69_out_6, black_01_69_out_7,
       black_01_69_out_8, black_01_70_out_5, black_01_70_out_6, black_01_70_out_7, black_01_70_out_8,
       black_01_71_out_5, black_01_71_out_6, black_01_71_out_7, black_01_71_out_8, black_02_1_b,
       black_02_1_c, black_02_2_b, black_02_2_c, black_02_3_b, black_02_3_c, black_02_4_b, black_02_4_c,
       black_02_5_b, black_02_5_c, black_02_6_b, black_02_6_c, black_02_7_b, black_02_7_c, black_02_8_b,
       black_02_8_c, black_02_9_b, black_02_9_c, black_02_10_b, black_02_10_c, black_02_11_b, black_02_11_c,
       black_02_12_b, black_02_12_c, black_02_13_b, black_02_13_c, black_02_14_b, black_02_14_c,
       black_02_15_b, black_02_15_c, black_02_16_b, black_02_16_c, black_02_17_b, black_02_17_c,
       black_02_18_b, black_02_18_c, black_02_19_b, black_02_19_c, black_02_20_b, black_02_20_c,
       black_02_21_b, black_02_21_c, black_02_22_b, black_02_22_c, black_02_23_b, black_02_23_c,
       black_02_24_b, black_02_24_c, black_02_25_b, black_02_25_c, black_02_26_b, black_02_26_c,
       black_02_27_b, black_02_27_c, black_02_28_b, black_02_28_c, black_02_29_b, black_02_29_c,
       black_02_30_b, black_02_30_c, black_02_31_b, black_02_31_c, grey_01_1_out_3, grey_01_1_out_4,
       grey_01_1_out_5, grey_01_1_out_6, grey_01_1_out_7, grey_01_2_out_3, grey_01_2_out_4, grey_01_2_out_5,
       grey_01_2_out_6, grey_01_2_out_7, grey_01_3_out_3, grey_01_3_out_4, grey_01_3_out_5, grey_01_3_out_6,
       grey_01_3_out_7, grey_01_4_out_3, grey_01_4_out_4, grey_01_4_out_5, grey_01_4_out_6, grey_01_4_out_7,
       grey_01_5_out_3, grey_01_5_out_4, grey_01_5_out_5, grey_01_5_out_6, grey_01_5_out_7, grey_01_6_out_3,
       grey_01_6_out_4, grey_01_6_out_5, grey_01_6_out_6, grey_01_6_out_7, grey_01_7_out_3, grey_01_7_out_4,
       grey_01_7_out_5, grey_01_7_out_6, grey_01_7_out_7, grey_01_8_out_3, grey_01_8_out_4, grey_01_8_out_5,
       grey_01_8_out_6, grey_01_8_out_7, grey_01_9_out_3, grey_01_9_out_4, grey_01_9_out_5, grey_01_9_out_6,
       grey_01_9_out_7, grey_01_10_out_3, grey_01_10_out_4, grey_01_10_out_5, grey_01_10_out_6,
       grey_01_10_out_7, grey_01_11_out_3, grey_01_11_out_4, grey_01_11_out_5, grey_01_11_out_6,
       grey_01_11_out_7, grey_01_12_out_3, grey_01_12_out_4, grey_01_12_out_5, grey_01_12_out_6,
       grey_01_12_out_7, grey_01_13_out_3, grey_01_13_out_4, grey_01_13_out_5, grey_01_13_out_6,
       grey_01_13_out_7, grey_01_14_out_3, grey_01_14_out_4, grey_01_14_out_5, grey_01_14_out_6,
       grey_01_14_out_7, grey_01_15_out_3, grey_01_15_out_4, grey_01_15_out_5, grey_01_15_out_6,
       grey_01_15_out_7, grey_01_16_out_3, grey_01_16_out_4, grey_01_16_out_5, grey_01_16_out_6,
       grey_01_16_out_7, grey_01_17_out_3, grey_01_17_out_4, grey_01_17_out_5, grey_01_17_out_6,
       grey_01_17_out_7, grey_01_18_out_3, grey_01_18_out_4, grey_01_18_out_5, grey_01_18_out_6,
       grey_01_18_out_7, grey_01_19_out_3, grey_01_19_out_4, grey_01_19_out_5, grey_01_19_out_6,
       grey_01_19_out_7, grey_01_20_out_3, grey_01_20_out_4, grey_01_20_out_5, grey_01_20_out_6,
       grey_01_20_out_7, grey_01_21_out_3, grey_01_21_out_4, grey_01_21_out_5, grey_01_21_out_6,
       grey_01_21_out_7, grey_01_22_out_3, grey_01_22_out_4, grey_01_22_out_5, grey_01_22_out_6,
       grey_01_22_out_7, grey_01_23_out_3, grey_01_23_out_4, grey_01_23_out_5, grey_01_23_out_6,
       grey_01_23_out_7, grey_01_24_out_3, grey_01_24_out_4, grey_01_24_out_5, grey_01_24_out_6,
       grey_01_24_out_7, grey_01_25_out_3, grey_01_25_out_4, grey_01_25_out_5, grey_01_25_out_6,
       grey_01_25_out_7, grey_01_26_out_3, grey_01_26_out_4, grey_01_26_out_5, grey_01_26_out_6,
       grey_01_26_out_7, grey_01_27_out_3, grey_01_27_out_4, grey_01_27_out_5, grey_01_27_out_6,
       grey_01_27_out_7, grey_01_28_out_3, grey_01_28_out_4, grey_01_28_out_5, grey_01_28_out_6,
       grey_01_28_out_7, grey_01_29_out_3, grey_01_29_out_4, grey_01_29_out_5, grey_01_29_out_6,
       grey_01_29_out_7, grey_01_30_out_3, grey_01_30_out_4, grey_01_30_out_5, grey_01_30_out_6,
       grey_01_30_out_7, grey_01_31_out_3, grey_01_31_out_4, grey_01_31_out_5, grey_01_31_out_6,
       grey_01_31_out_7, grey_02_1_out_3, grey_02_1_out_4, grey_02_1_out_5, maroon_00_1_out_4,
       maroon_00_2_out_4, maroon_00_3_out_4, maroon_00_4_out_4, maroon_00_5_out_4, maroon_00_6_out_4,
       maroon_00_7_out_4, maroon_00_8_out_4, maroon_00_9_out_4, maroon_00_10_out_4, maroon_00_11_out_4,
       maroon_00_12_out_4, maroon_00_13_out_4, maroon_00_14_out_4, maroon_00_15_out_4, maroon_00_16_out_4,
       maroon_00_17_out_4, maroon_00_18_out_4, maroon_00_19_out_4, maroon_00_20_out_4, maroon_00_21_out_4,
       maroon_00_22_out_4, maroon_00_23_out_4, maroon_00_24_out_4, maroon_00_25_out_4, maroon_00_26_out_4,
       maroon_00_27_out_4, maroon_00_28_out_4, maroon_00_29_out_4, maroon_00_30_out_4, maroon_00_31_out_4,
       maroon_00_32_out_4;
  wire [31:0] multiplexer_1_out, not_1_out;

  assign not_1_out = ~B;  // NOT_Gate not_1, 32 bits wide
  Multiplexer #(.width(32)) multiplexer_1 (.in0(B), .in1(not_1_out), .out(multiplexer_1_out), .sel(Subtraction));
  Grey_02 grey_02_1 (
    .in_1(multiplexer_1_out[31]), .in_2(A[31]), .out_3(grey_02_1_out_3), .out_4(grey_02_1_out_4),
    .out_5(grey_02_1_out_5));
  Black_02 black_02_1 (
    .in_2(grey_01_1_out_4), .in_3(grey_02_1_out_4), .in_4(grey_01_1_out_7), .in_1(grey_02_1_out_3),
    .b(black_02_1_b), .c(black_02_1_c));
  Black_02 black_02_2 (
    .in_2(black_01_1_out_6), .in_3(black_02_1_c), .in_4(black_01_1_out_8), .in_1(black_02_1_b),
    .b(black_02_2_b), .c(black_02_2_c));
  Black_02 black_02_3 (
    .in_2(black_01_4_out_6), .in_3(black_02_2_c), .in_4(black_01_4_out_8), .in_1(black_02_2_b),
    .b(black_02_3_b), .c(black_02_3_c));
  Black_02 black_02_4 (
    .in_2(black_01_13_out_6), .in_3(black_02_3_c), .in_4(black_01_13_out_8), .in_1(black_02_3_b),
    .b(black_02_4_b), .c(black_02_4_c));
  Maroon_00 maroon_00_1 (
    .in_1(black_02_4_b), .in_2(maroon_00_17_out_4), .in_3(black_02_4_c), .out_4(maroon_00_1_out_4));
  xor xor_1 (Carry, 1'b0, maroon_00_1_out_4);
  xor xor_2 (Result[31], grey_02_1_out_5, maroon_00_2_out_4);
  Grey_01 grey_01_1 (
    .in_1(multiplexer_1_out[30]), .in_2(A[30]), .out_3(grey_01_1_out_3), .out_4(grey_01_1_out_4),
    .out_5(grey_01_1_out_5), .out_6(grey_01_1_out_6), .out_7(grey_01_1_out_7));
  Black_02 black_02_5 (
    .in_2(grey_01_2_out_4), .in_3(grey_01_1_out_5), .in_4(grey_01_2_out_7), .in_1(grey_01_1_out_3),
    .b(black_02_5_b), .c(black_02_5_c));
  Black_02 black_02_6 (
    .in_2(black_01_2_out_6), .in_3(black_02_5_c), .in_4(black_01_2_out_8), .in_1(black_02_5_b),
    .b(black_02_6_b), .c(black_02_6_c));
  Black_02 black_02_7 (
    .in_2(black_01_6_out_6), .in_3(black_02_6_c), .in_4(black_01_6_out_8), .in_1(black_02_6_b),
    .b(black_02_7_b), .c(black_02_7_c));
  Black_02 black_02_8 (
    .in_2(black_01_16_out_6), .in_3(black_02_7_c), .in_4(black_01_16_out_8), .in_1(black_02_7_b),
    .b(black_02_8_b), .c(black_02_8_c));
  Maroon_00 maroon_00_2 (
    .in_1(black_02_8_b), .in_2(maroon_00_18_out_4), .in_3(black_02_8_c), .out_4(maroon_00_2_out_4));
  Grey_01 grey_01_2 (
    .in_1(multiplexer_1_out[29]), .in_2(A[29]), .out_3(grey_01_2_out_3), .out_4(grey_01_2_out_4),
    .out_5(grey_01_2_out_5), .out_6(grey_01_2_out_6), .out_7(grey_01_2_out_7));
  Black_01 black_01_1 (
    .in_2(grey_01_3_out_4), .in_3(grey_01_2_out_5), .in_4(grey_01_3_out_7), .in_1(grey_01_2_out_3),
    .out_5(black_01_1_out_5), .out_6(black_01_1_out_6), .out_7(black_01_1_out_7), .out_8(black_01_1_out_8));
  Black_02 black_02_9 (
    .in_2(black_01_3_out_6), .in_3(black_01_1_out_7), .in_4(black_01_3_out_8), .in_1(black_01_1_out_5),
    .b(black_02_9_b), .c(black_02_9_c));
  Black_02 black_02_10 (
    .in_2(black_01_8_out_6), .in_3(black_02_9_c), .in_4(black_01_8_out_8), .in_1(black_02_9_b),
    .b(black_02_10_b), .c(black_02_10_c));
  Black_02 black_02_11 (
    .in_2(black_01_19_out_6), .in_3(black_02_10_c), .in_4(black_01_19_out_8), .in_1(black_02_10_b),
    .b(black_02_11_b), .c(black_02_11_c));
  Maroon_00 maroon_00_3 (
    .in_1(black_02_11_b), .in_2(maroon_00_19_out_4), .in_3(black_02_11_c), .out_4(maroon_00_3_out_4));
  xor xor_3 (Result[30], grey_01_1_out_6, maroon_00_3_out_4);
  Grey_01 grey_01_3 (
    .in_1(multiplexer_1_out[28]), .in_2(A[28]), .out_3(grey_01_3_out_3), .out_4(grey_01_3_out_4),
    .out_5(grey_01_3_out_5), .out_6(grey_01_3_out_6), .out_7(grey_01_3_out_7));
  Black_01 black_01_2 (
    .in_2(grey_01_4_out_4), .in_3(grey_01_3_out_5), .in_4(grey_01_4_out_7), .in_1(grey_01_3_out_3),
    .out_5(black_01_2_out_5), .out_6(black_01_2_out_6), .out_7(black_01_2_out_7), .out_8(black_01_2_out_8));
  Black_02 black_02_12 (
    .in_2(black_01_5_out_6), .in_3(black_01_2_out_7), .in_4(black_01_5_out_8), .in_1(black_01_2_out_5),
    .b(black_02_12_b), .c(black_02_12_c));
  Black_02 black_02_13 (
    .in_2(black_01_10_out_6), .in_3(black_02_12_c), .in_4(black_01_10_out_8), .in_1(black_02_12_b),
    .b(black_02_13_b), .c(black_02_13_c));
  Black_02 black_02_14 (
    .in_2(black_01_22_out_6), .in_3(black_02_13_c), .in_4(black_01_22_out_8), .in_1(black_02_13_b),
    .b(black_02_14_b), .c(black_02_14_c));
  Maroon_00 maroon_00_4 (
    .in_1(black_02_14_b), .in_2(maroon_00_20_out_4), .in_3(black_02_14_c), .out_4(maroon_00_4_out_4));
  xor xor_4 (Result[29], grey_01_2_out_6, maroon_00_4_out_4);
  Grey_01 grey_01_4 (
    .in_1(multiplexer_1_out[27]), .in_2(A[27]), .out_3(grey_01_4_out_3), .out_4(grey_01_4_out_4),
    .out_5(grey_01_4_out_5), .out_6(grey_01_4_out_6), .out_7(grey_01_4_out_7));
  Black_01 black_01_3 (
    .in_2(grey_01_5_out_4), .in_3(grey_01_4_out_5), .in_4(grey_01_5_out_7), .in_1(grey_01_4_out_3),
    .out_5(black_01_3_out_5), .out_6(black_01_3_out_6), .out_7(black_01_3_out_7), .out_8(black_01_3_out_8));
  Black_01 black_01_4 (
    .in_2(black_01_7_out_6), .in_3(black_01_3_out_7), .in_4(black_01_7_out_8), .in_1(black_01_3_out_5),
    .out_5(black_01_4_out_5), .out_6(black_01_4_out_6), .out_7(black_01_4_out_7), .out_8(black_01_4_out_8));
  Black_02 black_02_15 (
    .in_2(black_01_12_out_6), .in_3(black_01_4_out_7), .in_4(black_01_12_out_8), .in_1(black_01_4_out_5),
    .b(black_02_15_b), .c(black_02_15_c));
  Black_02 black_02_16 (
    .in_2(black_01_25_out_6), .in_3(black_02_15_c), .in_4(black_01_25_out_8), .in_1(black_02_15_b),
    .b(black_02_16_b), .c(black_02_16_c));
  Maroon_00 maroon_00_5 (
    .in_1(black_02_16_b), .in_2(maroon_00_21_out_4), .in_3(black_02_16_c), .out_4(maroon_00_5_out_4));
  xor xor_5 (Result[28], grey_01_3_out_6, maroon_00_5_out_4);
  xor xor_6 (Result[27], grey_01_4_out_6, maroon_00_6_out_4);
  Grey_01 grey_01_5 (
    .in_1(multiplexer_1_out[26]), .in_2(A[26]), .out_3(grey_01_5_out_3), .out_4(grey_01_5_out_4),
    .out_5(grey_01_5_out_5), .out_6(grey_01_5_out_6), .out_7(grey_01_5_out_7));
  Black_01 black_01_5 (
    .in_2(grey_01_6_out_4), .in_3(grey_01_5_out_5), .in_4(grey_01_6_out_7), .in_1(grey_01_5_out_3),
    .out_5(black_01_5_out_5), .out_6(black_01_5_out_6), .out_7(black_01_5_out_7), .out_8(black_01_5_out_8));
  Black_01 black_01_6 (
    .in_2(black_01_9_out_6), .in_3(black_01_5_out_7), .in_4(black_01_9_out_8), .in_1(black_01_5_out_5),
    .out_5(black_01_6_out_5), .out_6(black_01_6_out_6), .out_7(black_01_6_out_7), .out_8(black_01_6_out_8));
  Black_02 black_02_17 (
    .in_2(black_01_15_out_6), .in_3(black_01_6_out_7), .in_4(black_01_15_out_8), .in_1(black_01_6_out_5),
    .b(black_02_17_b), .c(black_02_17_c));
  Black_02 black_02_18 (
    .in_2(black_01_28_out_6), .in_3(black_02_17_c), .in_4(black_01_28_out_8), .in_1(black_02_17_b),
    .b(black_02_18_b), .c(black_02_18_c));
  Maroon_00 maroon_00_6 (
    .in_1(black_02_18_b), .in_2(maroon_00_22_out_4), .in_3(black_02_18_c), .out_4(maroon_00_6_out_4));
  Grey_01 grey_01_6 (
    .in_1(multiplexer_1_out[25]), .in_2(A[25]), .out_3(grey_01_6_out_3), .out_4(grey_01_6_out_4),
    .out_5(grey_01_6_out_5), .out_6(grey_01_6_out_6), .out_7(grey_01_6_out_7));
  Black_01 black_01_7 (
    .in_2(grey_01_7_out_4), .in_3(grey_01_6_out_5), .in_4(grey_01_7_out_7), .in_1(grey_01_6_out_3),
    .out_5(black_01_7_out_5), .out_6(black_01_7_out_6), .out_7(black_01_7_out_7), .out_8(black_01_7_out_8));
  Black_01 black_01_8 (
    .in_2(black_01_11_out_6), .in_3(black_01_7_out_7), .in_4(black_01_11_out_8), .in_1(black_01_7_out_5),
    .out_5(black_01_8_out_5), .out_6(black_01_8_out_6), .out_7(black_01_8_out_7), .out_8(black_01_8_out_8));
  Black_02 black_02_19 (
    .in_2(black_01_18_out_6), .in_3(black_01_8_out_7), .in_4(black_01_18_out_8), .in_1(black_01_8_out_5),
    .b(black_02_19_b), .c(black_02_19_c));
  Black_02 black_02_20 (
    .in_2(black_01_31_out_6), .in_3(black_02_19_c), .in_4(black_01_31_out_8), .in_1(black_02_19_b),
    .b(black_02_20_b), .c(black_02_20_c));
  Maroon_00 maroon_00_7 (
    .in_1(black_02_20_b), .in_2(maroon_00_23_out_4), .in_3(black_02_20_c), .out_4(maroon_00_7_out_4));
  xor xor_7 (Result[26], grey_01_5_out_6, maroon_00_7_out_4);
  Grey_01 grey_01_7 (
    .in_1(multiplexer_1_out[24]), .in_2(A[24]), .out_3(grey_01_7_out_3), .out_4(grey_01_7_out_4),
    .out_5(grey_01_7_out_5), .out_6(grey_01_7_out_6), .out_7(grey_01_7_out_7));
  Black_01 black_01_9 (
    .in_2(grey_01_8_out_4), .in_3(grey_01_7_out_5), .in_4(grey_01_8_out_7), .in_1(grey_01_7_out_3),
    .out_5(black_01_9_out_5), .out_6(black_01_9_out_6), .out_7(black_01_9_out_7), .out_8(black_01_9_out_8));
  Black_01 black_01_10 (
    .in_2(black_01_14_out_6), .in_3(black_01_9_out_7), .in_4(black_01_14_out_8), .in_1(black_01_9_out_5),
    .out_5(black_01_10_out_5), .out_6(black_01_10_out_6), .out_7(black_01_10_out_7), .out_8(black_01_10_out_8));
  Black_02 black_02_21 (
    .in_2(black_01_21_out_6), .in_3(black_01_10_out_7), .in_4(black_01_21_out_8), .in_1(black_01_10_out_5),
    .b(black_02_21_b), .c(black_02_21_c));
  Black_02 black_02_22 (
    .in_2(black_01_34_out_6), .in_3(black_02_21_c), .in_4(black_01_34_out_8), .in_1(black_02_21_b),
    .b(black_02_22_b), .c(black_02_22_c));
  Maroon_00 maroon_00_8 (
    .in_1(black_02_22_b), .in_2(maroon_00_24_out_4), .in_3(black_02_22_c), .out_4(maroon_00_8_out_4));
  xor xor_8 (Result[25], grey_01_6_out_6, maroon_00_8_out_4);
  Grey_01 grey_01_8 (
    .in_1(multiplexer_1_out[23]), .in_2(A[23]), .out_3(grey_01_8_out_3), .out_4(grey_01_8_out_4),
    .out_5(grey_01_8_out_5), .out_6(grey_01_8_out_6), .out_7(grey_01_8_out_7));
  Black_01 black_01_11 (
    .in_2(grey_01_9_out_4), .in_3(grey_01_8_out_5), .in_4(grey_01_9_out_7), .in_1(grey_01_8_out_3),
    .out_5(black_01_11_out_5), .out_6(black_01_11_out_6), .out_7(black_01_11_out_7), .out_8(black_01_11_out_8));
  Black_01 black_01_12 (
    .in_2(black_01_17_out_6), .in_3(black_01_11_out_7), .in_4(black_01_17_out_8), .in_1(black_01_11_out_5),
    .out_5(black_01_12_out_5), .out_6(black_01_12_out_6), .out_7(black_01_12_out_7), .out_8(black_01_12_out_8));
  Black_01 black_01_13 (
    .in_2(black_01_24_out_6), .in_3(black_01_12_out_7), .in_4(black_01_24_out_8), .in_1(black_01_12_out_5),
    .out_5(black_01_13_out_5), .out_6(black_01_13_out_6), .out_7(black_01_13_out_7), .out_8(black_01_13_out_8));
  Black_02 black_02_23 (
    .in_2(black_01_37_out_6), .in_3(black_01_13_out_7), .in_4(black_01_37_out_8), .in_1(black_01_13_out_5),
    .b(black_02_23_b), .c(black_02_23_c));
  Maroon_00 maroon_00_9 (
    .in_1(black_02_23_b), .in_2(maroon_00_25_out_4), .in_3(black_02_23_c), .out_4(maroon_00_9_out_4));
  xor xor_9 (Result[24], grey_01_7_out_6, maroon_00_9_out_4);
  xor xor_10 (Result[23], grey_01_8_out_6, maroon_00_10_out_4);
  Grey_01 grey_01_9 (
    .in_1(multiplexer_1_out[22]), .in_2(A[22]), .out_3(grey_01_9_out_3), .out_4(grey_01_9_out_4),
    .out_5(grey_01_9_out_5), .out_6(grey_01_9_out_6), .out_7(grey_01_9_out_7));
  Black_01 black_01_14 (
    .in_2(grey_01_10_out_4), .in_3(grey_01_9_out_5), .in_4(grey_01_10_out_7), .in_1(grey_01_9_out_3),
    .out_5(black_01_14_out_5), .out_6(black_01_14_out_6), .out_7(black_01_14_out_7), .out_8(black_01_14_out_8));
  Black_01 black_01_15 (
    .in_2(black_01_20_out_6), .in_3(black_01_14_out_7), .in_4(black_01_20_out_8), .in_1(black_01_14_out_5),
    .out_5(black_01_15_out_5), .out_6(black_01_15_out_6), .out_7(black_01_15_out_7), .out_8(black_01_15_out_8));
  Black_01 black_01_16 (
    .in_2(black_01_27_out_6), .in_3(black_01_15_out_7), .in_4(black_01_27_out_8), .in_1(black_01_15_out_5),
    .out_5(black_01_16_out_5), .out_6(black_01_16_out_6), .out_7(black_01_16_out_7), .out_8(black_01_16_out_8));
  Black_02 black_02_24 (
    .in_2(black_01_40_out_6), .in_3(black_01_16_out_7), .in_4(black_01_40_out_8), .in_1(black_01_16_out_5),
    .b(black_02_24_b), .c(black_02_24_c));
  Maroon_00 maroon_00_10 (
    .in_1(black_02_24_b), .in_2(maroon_00_26_out_4), .in_3(black_02_24_c), .out_4(maroon_00_10_out_4));
  Grey_01 grey_01_10 (
    .in_1(multiplexer_1_out[21]), .in_2(A[21]), .out_3(grey_01_10_out_3), .out_4(grey_01_10_out_4),
    .out_5(grey_01_10_out_5), .out_6(grey_01_10_out_6), .out_7(grey_01_10_out_7));
  Black_01 black_01_17 (
    .in_2(grey_01_11_out_4), .in_3(grey_01_10_out_5), .in_4(grey_01_11_out_7), .in_1(grey_01_10_out_3),
    .out_5(black_01_17_out_5), .out_6(black_01_17_out_6), .out_7(black_01_17_out_7), .out_8(black_01_17_out_8));
  Black_01 black_01_18 (
    .in_2(black_01_23_out_6), .in_3(black_01_17_out_7), .in_4(black_01_23_out_8), .in_1(black_01_17_out_5),
    .out_5(black_01_18_out_5), .out_6(black_01_18_out_6), .out_7(black_01_18_out_7), .out_8(black_01_18_out_8));
  Black_01 black_01_19 (
    .in_2(black_01_30_out_6), .in_3(black_01_18_out_7), .in_4(black_01_30_out_8), .in_1(black_01_18_out_5),
    .out_5(black_01_19_out_5), .out_6(black_01_19_out_6), .out_7(black_01_19_out_7), .out_8(black_01_19_out_8));
  Black_02 black_02_25 (
    .in_2(black_01_43_out_6), .in_3(black_01_19_out_7), .in_4(black_01_43_out_8), .in_1(black_01_19_out_5),
    .b(black_02_25_b), .c(black_02_25_c));
  Maroon_00 maroon_00_11 (
    .in_1(black_02_25_b), .in_2(maroon_00_27_out_4), .in_3(black_02_25_c), .out_4(maroon_00_11_out_4));
  xor xor_11 (Result[22], grey_01_9_out_6, maroon_00_11_out_4);
  Grey_01 grey_01_11 (
    .in_1(multiplexer_1_out[20]), .in_2(A[20]), .out_3(grey_01_11_out_3), .out_4(grey_01_11_out_4),
    .out_5(grey_01_11_out_5), .out_6(grey_01_11_out_6), .out_7(grey_01_11_out_7));
  Black_01 black_01_20 (
    .in_2(grey_01_12_out_4), .in_3(grey_01_11_out_5), .in_4(grey_01_12_out_7), .in_1(grey_01_11_out_3),
    .out_5(black_01_20_out_5), .out_6(black_01_20_out_6), .out_7(black_01_20_out_7), .out_8(black_01_20_out_8));
  Black_01 black_01_21 (
    .in_2(black_01_26_out_6), .in_3(black_01_20_out_7), .in_4(black_01_26_out_8), .in_1(black_01_20_out_5),
    .out_5(black_01_21_out_5), .out_6(black_01_21_out_6), .out_7(black_01_21_out_7), .out_8(black_01_21_out_8));
  Black_01 black_01_22 (
    .in_2(black_01_33_out_6), .in_3(black_01_21_out_7), .in_4(black_01_33_out_8), .in_1(black_01_21_out_5),
    .out_5(black_01_22_out_5), .out_6(black_01_22_out_6), .out_7(black_01_22_out_7), .out_8(black_01_22_out_8));
  Black_02 black_02_26 (
    .in_2(black_01_46_out_6), .in_3(black_01_22_out_7), .in_4(black_01_46_out_8), .in_1(black_01_22_out_5),
    .b(black_02_26_b), .c(black_02_26_c));
  Maroon_00 maroon_00_12 (
    .in_1(black_02_26_b), .in_2(maroon_00_28_out_4), .in_3(black_02_26_c), .out_4(maroon_00_12_out_4));
  xor xor_12 (Result[21], grey_01_10_out_6, maroon_00_12_out_4);
  xor xor_13 (Result[20], grey_01_11_out_6, maroon_00_13_out_4);
  Grey_01 grey_01_12 (
    .in_1(multiplexer_1_out[19]), .in_2(A[19]), .out_3(grey_01_12_out_3), .out_4(grey_01_12_out_4),
    .out_5(grey_01_12_out_5), .out_6(grey_01_12_out_6), .out_7(grey_01_12_out_7));
  Black_01 black_01_23 (
    .in_2(grey_01_13_out_4), .in_3(grey_01_12_out_5), .in_4(grey_01_13_out_7), .in_1(grey_01_12_out_3),
    .out_5(black_01_23_out_5), .out_6(black_01_23_out_6), .out_7(black_01_23_out_7), .out_8(black_01_23_out_8));
  Black_01 black_01_24 (
    .in_2(black_01_29_out_6), .in_3(black_01_23_out_7), .in_4(black_01_29_out_8), .in_1(black_01_23_out_5),
    .out_5(black_01_24_out_5), .out_6(black_01_24_out_6), .out_7(black_01_24_out_7), .out_8(black_01_24_out_8));
  Black_01 black_01_25 (
    .in_2(black_01_36_out_6), .in_3(black_01_24_out_7), .in_4(black_01_36_out_8), .in_1(black_01_24_out_5),
    .out_5(black_01_25_out_5), .out_6(black_01_25_out_6), .out_7(black_01_25_out_7), .out_8(black_01_25_out_8));
  Black_02 black_02_27 (
    .in_2(black_01_49_out_6), .in_3(black_01_25_out_7), .in_4(black_01_49_out_8), .in_1(black_01_25_out_5),
    .b(black_02_27_b), .c(black_02_27_c));
  Maroon_00 maroon_00_13 (
    .in_1(black_02_27_b), .in_2(maroon_00_29_out_4), .in_3(black_02_27_c), .out_4(maroon_00_13_out_4));
  Grey_01 grey_01_13 (
    .in_1(multiplexer_1_out[18]), .in_2(A[18]), .out_3(grey_01_13_out_3), .out_4(grey_01_13_out_4),
    .out_5(grey_01_13_out_5), .out_6(grey_01_13_out_6), .out_7(grey_01_13_out_7));
  Black_01 black_01_26 (
    .in_2(grey_01_14_out_4), .in_3(grey_01_13_out_5), .in_4(grey_01_14_out_7), .in_1(grey_01_13_out_3),
    .out_5(black_01_26_out_5), .out_6(black_01_26_out_6), .out_7(black_01_26_out_7), .out_8(black_01_26_out_8));
  Black_01 black_01_27 (
    .in_2(black_01_32_out_6), .in_3(black_01_26_out_7), .in_4(black_01_32_out_8), .in_1(black_01_26_out_5),
    .out_5(black_01_27_out_5), .out_6(black_01_27_out_6), .out_7(black_01_27_out_7), .out_8(black_01_27_out_8));
  Black_01 black_01_28 (
    .in_2(black_01_39_out_6), .in_3(black_01_27_out_7), .in_4(black_01_39_out_8), .in_1(black_01_27_out_5),
    .out_5(black_01_28_out_5), .out_6(black_01_28_out_6), .out_7(black_01_28_out_7), .out_8(black_01_28_out_8));
  Black_02 black_02_28 (
    .in_2(black_01_52_out_6), .in_3(black_01_28_out_7), .in_4(black_01_52_out_8), .in_1(black_01_28_out_5),
    .b(black_02_28_b), .c(black_02_28_c));
  Maroon_00 maroon_00_14 (
    .in_1(black_02_28_b), .in_2(maroon_00_30_out_4), .in_3(black_02_28_c), .out_4(maroon_00_14_out_4));
  xor xor_14 (Result[19], grey_01_12_out_6, maroon_00_14_out_4);
  Grey_01 grey_01_14 (
    .in_1(multiplexer_1_out[17]), .in_2(A[17]), .out_3(grey_01_14_out_3), .out_4(grey_01_14_out_4),
    .out_5(grey_01_14_out_5), .out_6(grey_01_14_out_6), .out_7(grey_01_14_out_7));
  Black_01 black_01_29 (
    .in_2(grey_01_15_out_4), .in_3(grey_01_14_out_5), .in_4(grey_01_15_out_7), .in_1(grey_01_14_out_3),
    .out_5(black_01_29_out_5), .out_6(black_01_29_out_6), .out_7(black_01_29_out_7), .out_8(black_01_29_out_8));
  Black_01 black_01_30 (
    .in_2(black_01_35_out_6), .in_3(black_01_29_out_7), .in_4(black_01_35_out_8), .in_1(black_01_29_out_5),
    .out_5(black_01_30_out_5), .out_6(black_01_30_out_6), .out_7(black_01_30_out_7), .out_8(black_01_30_out_8));
  Black_01 black_01_31 (
    .in_2(black_01_42_out_6), .in_3(black_01_30_out_7), .in_4(black_01_42_out_8), .in_1(black_01_30_out_5),
    .out_5(black_01_31_out_5), .out_6(black_01_31_out_6), .out_7(black_01_31_out_7), .out_8(black_01_31_out_8));
  Black_02 black_02_29 (
    .in_2(black_01_55_out_6), .in_3(black_01_31_out_7), .in_4(black_01_55_out_8), .in_1(black_01_31_out_5),
    .b(black_02_29_b), .c(black_02_29_c));
  Maroon_00 maroon_00_15 (
    .in_1(black_02_29_b), .in_2(maroon_00_31_out_4), .in_3(black_02_29_c), .out_4(maroon_00_15_out_4));
  xor xor_15 (Result[18], grey_01_13_out_6, maroon_00_15_out_4);
  Grey_01 grey_01_15 (
    .in_1(multiplexer_1_out[16]), .in_2(A[16]), .out_3(grey_01_15_out_3), .out_4(grey_01_15_out_4),
    .out_5(grey_01_15_out_5), .out_6(grey_01_15_out_6), .out_7(grey_01_15_out_7));
  Black_01 black_01_32 (
    .in_2(grey_01_16_out_4), .in_3(grey_01_15_out_5), .in_4(grey_01_16_out_7), .in_1(grey_01_15_out_3),
    .out_5(black_01_32_out_5), .out_6(black_01_32_out_6), .out_7(black_01_32_out_7), .out_8(black_01_32_out_8));
  Black_01 black_01_33 (
    .in_2(black_01_38_out_6), .in_3(black_01_32_out_7), .in_4(black_01_38_out_8), .in_1(black_01_32_out_5),
    .out_5(black_01_33_out_5), .out_6(black_01_33_out_6), .out_7(black_01_33_out_7), .out_8(black_01_33_out_8));
  Black_01 black_01_34 (
    .in_2(black_01_45_out_6), .in_3(black_01_33_out_7), .in_4(black_01_45_out_8), .in_1(black_01_33_out_5),
    .out_5(black_01_34_out_5), .out_6(black_01_34_out_6), .out_7(black_01_34_out_7), .out_8(black_01_34_out_8));
  Black_02 black_02_30 (
    .in_2(black_01_58_out_6), .in_3(black_01_34_out_7), .in_4(black_01_58_out_8), .in_1(black_01_34_out_5),
    .b(black_02_30_b), .c(black_02_30_c));
  Maroon_00 maroon_00_16 (
    .in_1(black_02_30_b), .in_2(maroon_00_32_out_4), .in_3(black_02_30_c), .out_4(maroon_00_16_out_4));
  xor xor_16 (Result[17], grey_01_14_out_6, maroon_00_16_out_4);
  xor xor_17 (Result[16], grey_01_15_out_6, maroon_00_17_out_4);
  Grey_01 grey_01_16 (
    .in_1(multiplexer_1_out[15]), .in_2(A[15]), .out_3(grey_01_16_out_3), .out_4(grey_01_16_out_4),
    .out_5(grey_01_16_out_5), .out_6(grey_01_16_out_6), .out_7(grey_01_16_out_7));
  Black_01 black_01_35 (
    .in_2(grey_01_17_out_4), .in_3(grey_01_16_out_5), .in_4(grey_01_17_out_7), .in_1(grey_01_16_out_3),
    .out_5(black_01_35_out_5), .out_6(black_01_35_out_6), .out_7(black_01_35_out_7), .out_8(black_01_35_out_8));
  Black_01 black_01_36 (
    .in_2(black_01_41_out_6), .in_3(black_01_35_out_7), .in_4(black_01_41_out_8), .in_1(black_01_35_out_5),
    .out_5(black_01_36_out_5), .out_6(black_01_36_out_6), .out_7(black_01_36_out_7), .out_8(black_01_36_out_8));
  Black_01 black_01_37 (
    .in_2(black_01_48_out_6), .in_3(black_01_36_out_7), .in_4(black_01_48_out_8), .in_1(black_01_36_out_5),
    .out_5(black_01_37_out_5), .out_6(black_01_37_out_6), .out_7(black_01_37_out_7), .out_8(black_01_37_out_8));
  Black_02 black_02_31 (
    .in_2(black_01_61_out_6), .in_3(black_01_37_out_7), .in_4(black_01_61_out_8), .in_1(black_01_37_out_5),
    .b(black_02_31_b), .c(black_02_31_c));
  Maroon_00 maroon_00_17 (.in_1(black_02_31_b), .in_2(Subtraction), .in_3(black_02_31_c), .out_4(maroon_00_17_out_4));
  Grey_01 grey_01_17 (
    .in_1(multiplexer_1_out[14]), .in_2(A[14]), .out_3(grey_01_17_out_3), .out_4(grey_01_17_out_4),
    .out_5(grey_01_17_out_5), .out_6(grey_01_17_out_6), .out_7(grey_01_17_out_7));
  Black_01 black_01_38 (
    .in_2(grey_01_18_out_4), .in_3(grey_01_17_out_5), .in_4(grey_01_18_out_7), .in_1(grey_01_17_out_3),
    .out_5(black_01_38_out_5), .out_6(black_01_38_out_6), .out_7(black_01_38_out_7), .out_8(black_01_38_out_8));
  Black_01 black_01_39 (
    .in_2(black_01_44_out_6), .in_3(black_01_38_out_7), .in_4(black_01_44_out_8), .in_1(black_01_38_out_5),
    .out_5(black_01_39_out_5), .out_6(black_01_39_out_6), .out_7(black_01_39_out_7), .out_8(black_01_39_out_8));
  Black_01 black_01_40 (
    .in_2(black_01_51_out_6), .in_3(black_01_39_out_7), .in_4(black_01_51_out_8), .in_1(black_01_39_out_5),
    .out_5(black_01_40_out_5), .out_6(black_01_40_out_6), .out_7(black_01_40_out_7), .out_8(black_01_40_out_8));
  Maroon_00 maroon_00_18 (
    .in_1(black_01_40_out_5), .in_2(maroon_00_26_out_4), .in_3(black_01_40_out_7), .out_4(maroon_00_18_out_4));
  xor xor_18 (Result[15], grey_01_16_out_6, maroon_00_18_out_4);
  Grey_01 grey_01_18 (
    .in_1(multiplexer_1_out[13]), .in_2(A[13]), .out_3(grey_01_18_out_3), .out_4(grey_01_18_out_4),
    .out_5(grey_01_18_out_5), .out_6(grey_01_18_out_6), .out_7(grey_01_18_out_7));
  Black_01 black_01_41 (
    .in_2(grey_01_19_out_4), .in_3(grey_01_18_out_5), .in_4(grey_01_19_out_7), .in_1(grey_01_18_out_3),
    .out_5(black_01_41_out_5), .out_6(black_01_41_out_6), .out_7(black_01_41_out_7), .out_8(black_01_41_out_8));
  Black_01 black_01_42 (
    .in_2(black_01_47_out_6), .in_3(black_01_41_out_7), .in_4(black_01_47_out_8), .in_1(black_01_41_out_5),
    .out_5(black_01_42_out_5), .out_6(black_01_42_out_6), .out_7(black_01_42_out_7), .out_8(black_01_42_out_8));
  Black_01 black_01_43 (
    .in_2(black_01_54_out_6), .in_3(black_01_42_out_7), .in_4(black_01_54_out_8), .in_1(black_01_42_out_5),
    .out_5(black_01_43_out_5), .out_6(black_01_43_out_6), .out_7(black_01_43_out_7), .out_8(black_01_43_out_8));
  Maroon_00 maroon_00_19 (
    .in_1(black_01_43_out_5), .in_2(maroon_00_27_out_4), .in_3(black_01_43_out_7), .out_4(maroon_00_19_out_4));
  xor xor_19 (Result[14], grey_01_17_out_6, maroon_00_19_out_4);
  Grey_01 grey_01_19 (
    .in_1(multiplexer_1_out[12]), .in_2(A[12]), .out_3(grey_01_19_out_3), .out_4(grey_01_19_out_4),
    .out_5(grey_01_19_out_5), .out_6(grey_01_19_out_6), .out_7(grey_01_19_out_7));
  Black_01 black_01_44 (
    .in_2(grey_01_20_out_4), .in_3(grey_01_19_out_5), .in_4(grey_01_20_out_7), .in_1(grey_01_19_out_3),
    .out_5(black_01_44_out_5), .out_6(black_01_44_out_6), .out_7(black_01_44_out_7), .out_8(black_01_44_out_8));
  Black_01 black_01_45 (
    .in_2(black_01_50_out_6), .in_3(black_01_44_out_7), .in_4(black_01_50_out_8), .in_1(black_01_44_out_5),
    .out_5(black_01_45_out_5), .out_6(black_01_45_out_6), .out_7(black_01_45_out_7), .out_8(black_01_45_out_8));
  Black_01 black_01_46 (
    .in_2(black_01_57_out_6), .in_3(black_01_45_out_7), .in_4(black_01_57_out_8), .in_1(black_01_45_out_5),
    .out_5(black_01_46_out_5), .out_6(black_01_46_out_6), .out_7(black_01_46_out_7), .out_8(black_01_46_out_8));
  Maroon_00 maroon_00_20 (
    .in_1(black_01_46_out_5), .in_2(maroon_00_28_out_4), .in_3(black_01_46_out_7), .out_4(maroon_00_20_out_4));
  xor xor_20 (Result[13], grey_01_18_out_6, maroon_00_20_out_4);
  xor xor_21 (Result[12], grey_01_19_out_6, maroon_00_21_out_4);
  Grey_01 grey_01_20 (
    .in_1(multiplexer_1_out[11]), .in_2(A[11]), .out_3(grey_01_20_out_3), .out_4(grey_01_20_out_4),
    .out_5(grey_01_20_out_5), .out_6(grey_01_20_out_6), .out_7(grey_01_20_out_7));
  Black_01 black_01_47 (
    .in_2(grey_01_21_out_4), .in_3(grey_01_20_out_5), .in_4(grey_01_21_out_7), .in_1(grey_01_20_out_3),
    .out_5(black_01_47_out_5), .out_6(black_01_47_out_6), .out_7(black_01_47_out_7), .out_8(black_01_47_out_8));
  Black_01 black_01_48 (
    .in_2(black_01_53_out_6), .in_3(black_01_47_out_7), .in_4(black_01_53_out_8), .in_1(black_01_47_out_5),
    .out_5(black_01_48_out_5), .out_6(black_01_48_out_6), .out_7(black_01_48_out_7), .out_8(black_01_48_out_8));
  Black_01 black_01_49 (
    .in_2(black_01_60_out_6), .in_3(black_01_48_out_7), .in_4(black_01_60_out_8), .in_1(black_01_48_out_5),
    .out_5(black_01_49_out_5), .out_6(black_01_49_out_6), .out_7(black_01_49_out_7), .out_8(black_01_49_out_8));
  Maroon_00 maroon_00_21 (
    .in_1(black_01_49_out_5), .in_2(maroon_00_29_out_4), .in_3(black_01_49_out_7), .out_4(maroon_00_21_out_4));
  Grey_01 grey_01_21 (
    .in_1(multiplexer_1_out[10]), .in_2(A[10]), .out_3(grey_01_21_out_3), .out_4(grey_01_21_out_4),
    .out_5(grey_01_21_out_5), .out_6(grey_01_21_out_6), .out_7(grey_01_21_out_7));
  Black_01 black_01_50 (
    .in_2(grey_01_22_out_4), .in_3(grey_01_21_out_5), .in_4(grey_01_22_out_7), .in_1(grey_01_21_out_3),
    .out_5(black_01_50_out_5), .out_6(black_01_50_out_6), .out_7(black_01_50_out_7), .out_8(black_01_50_out_8));
  Black_01 black_01_51 (
    .in_2(black_01_56_out_6), .in_3(black_01_50_out_7), .in_4(black_01_56_out_8), .in_1(black_01_50_out_5),
    .out_5(black_01_51_out_5), .out_6(black_01_51_out_6), .out_7(black_01_51_out_7), .out_8(black_01_51_out_8));
  Black_01 black_01_52 (
    .in_2(black_01_63_out_6), .in_3(black_01_51_out_7), .in_4(black_01_63_out_8), .in_1(black_01_51_out_5),
    .out_5(black_01_52_out_5), .out_6(black_01_52_out_6), .out_7(black_01_52_out_7), .out_8(black_01_52_out_8));
  Maroon_00 maroon_00_22 (
    .in_1(black_01_52_out_5), .in_2(maroon_00_30_out_4), .in_3(black_01_52_out_7), .out_4(maroon_00_22_out_4));
  xor xor_22 (Result[11], grey_01_20_out_6, maroon_00_22_out_4);
  Grey_01 grey_01_22 (
    .in_1(multiplexer_1_out[9]), .in_2(A[9]), .out_3(grey_01_22_out_3), .out_4(grey_01_22_out_4),
    .out_5(grey_01_22_out_5), .out_6(grey_01_22_out_6), .out_7(grey_01_22_out_7));
  Black_01 black_01_53 (
    .in_2(grey_01_23_out_4), .in_3(grey_01_22_out_5), .in_4(grey_01_23_out_7), .in_1(grey_01_22_out_3),
    .out_5(black_01_53_out_5), .out_6(black_01_53_out_6), .out_7(black_01_53_out_7), .out_8(black_01_53_out_8));
  Black_01 black_01_54 (
    .in_2(black_01_59_out_6), .in_3(black_01_53_out_7), .in_4(black_01_59_out_8), .in_1(black_01_53_out_5),
    .out_5(black_01_54_out_5), .out_6(black_01_54_out_6), .out_7(black_01_54_out_7), .out_8(black_01_54_out_8));
  Black_01 black_01_55 (
    .in_2(black_01_65_out_6), .in_3(black_01_54_out_7), .in_4(black_01_65_out_8), .in_1(black_01_54_out_5),
    .out_5(black_01_55_out_5), .out_6(black_01_55_out_6), .out_7(black_01_55_out_7), .out_8(black_01_55_out_8));
  Maroon_00 maroon_00_23 (
    .in_1(black_01_55_out_5), .in_2(maroon_00_31_out_4), .in_3(black_01_55_out_7), .out_4(maroon_00_23_out_4));
  xor xor_23 (Result[10], grey_01_21_out_6, maroon_00_23_out_4);
  Grey_01 grey_01_23 (
    .in_1(multiplexer_1_out[8]), .in_2(A[8]), .out_3(grey_01_23_out_3), .out_4(grey_01_23_out_4),
    .out_5(grey_01_23_out_5), .out_6(grey_01_23_out_6), .out_7(grey_01_23_out_7));
  Black_01 black_01_56 (
    .in_2(grey_01_24_out_4), .in_3(grey_01_23_out_5), .in_4(grey_01_24_out_7), .in_1(grey_01_23_out_3),
    .out_5(black_01_56_out_5), .out_6(black_01_56_out_6), .out_7(black_01_56_out_7), .out_8(black_01_56_out_8));
  Black_01 black_01_57 (
    .in_2(black_01_62_out_6), .in_3(black_01_56_out_7), .in_4(black_01_62_out_8), .in_1(black_01_56_out_5),
    .out_5(black_01_57_out_5), .out_6(black_01_57_out_6), .out_7(black_01_57_out_7), .out_8(black_01_57_out_8));
  Black_01 black_01_58 (
    .in_2(black_01_67_out_6), .in_3(black_01_57_out_7), .in_4(black_01_67_out_8), .in_1(black_01_57_out_5),
    .out_5(black_01_58_out_5), .out_6(black_01_58_out_6), .out_7(black_01_58_out_7), .out_8(black_01_58_out_8));
  Maroon_00 maroon_00_24 (
    .in_1(black_01_58_out_5), .in_2(maroon_00_32_out_4), .in_3(black_01_58_out_7), .out_4(maroon_00_24_out_4));
  xor xor_24 (Result[9], grey_01_22_out_6, maroon_00_24_out_4);
  xor xor_25 (Result[8], grey_01_23_out_6, maroon_00_25_out_4);
  Grey_01 grey_01_24 (
    .in_1(multiplexer_1_out[7]), .in_2(A[7]), .out_3(grey_01_24_out_3), .out_4(grey_01_24_out_4),
    .out_5(grey_01_24_out_5), .out_6(grey_01_24_out_6), .out_7(grey_01_24_out_7));
  Black_01 black_01_59 (
    .in_2(grey_01_25_out_4), .in_3(grey_01_24_out_5), .in_4(grey_01_25_out_7), .in_1(grey_01_24_out_3),
    .out_5(black_01_59_out_5), .out_6(black_01_59_out_6), .out_7(black_01_59_out_7), .out_8(black_01_59_out_8));
  Black_01 black_01_60 (
    .in_2(black_01_64_out_6), .in_3(black_01_59_out_7), .in_4(black_01_64_out_8), .in_1(black_01_59_out_5),
    .out_5(black_01_60_out_5), .out_6(black_01_60_out_6), .out_7(black_01_60_out_7), .out_8(black_01_60_out_8));
  Black_01 black_01_61 (
    .in_2(black_01_69_out_6), .in_3(black_01_60_out_7), .in_4(black_01_69_out_8), .in_1(black_01_60_out_5),
    .out_5(black_01_61_out_5), .out_6(black_01_61_out_6), .out_7(black_01_61_out_7), .out_8(black_01_61_out_8));
  Maroon_00 maroon_00_25 (
    .in_1(black_01_61_out_5), .in_2(Subtraction), .in_3(black_01_61_out_7), .out_4(maroon_00_25_out_4));
  Grey_01 grey_01_25 (
    .in_1(multiplexer_1_out[6]), .in_2(A[6]), .out_3(grey_01_25_out_3), .out_4(grey_01_25_out_4),
    .out_5(grey_01_25_out_5), .out_6(grey_01_25_out_6), .out_7(grey_01_25_out_7));
  Black_01 black_01_62 (
    .in_2(grey_01_26_out_4), .in_3(grey_01_25_out_5), .in_4(grey_01_26_out_7), .in_1(grey_01_25_out_3),
    .out_5(black_01_62_out_5), .out_6(black_01_62_out_6), .out_7(black_01_62_out_7), .out_8(black_01_62_out_8));
  Black_01 black_01_63 (
    .in_2(black_01_66_out_6), .in_3(black_01_62_out_7), .in_4(black_01_66_out_8), .in_1(black_01_62_out_5),
    .out_5(black_01_63_out_5), .out_6(black_01_63_out_6), .out_7(black_01_63_out_7), .out_8(black_01_63_out_8));
  Maroon_00 maroon_00_26 (
    .in_1(black_01_63_out_5), .in_2(maroon_00_30_out_4), .in_3(black_01_63_out_7), .out_4(maroon_00_26_out_4));
  xor xor_26 (Result[7], grey_01_24_out_6, maroon_00_26_out_4);
  Grey_01 grey_01_26 (
    .in_1(multiplexer_1_out[5]), .in_2(A[5]), .out_3(grey_01_26_out_3), .out_4(grey_01_26_out_4),
    .out_5(grey_01_26_out_5), .out_6(grey_01_26_out_6), .out_7(grey_01_26_out_7));
  Black_01 black_01_64 (
    .in_2(grey_01_27_out_4), .in_3(grey_01_26_out_5), .in_4(grey_01_27_out_7), .in_1(grey_01_26_out_3),
    .out_5(black_01_64_out_5), .out_6(black_01_64_out_6), .out_7(black_01_64_out_7), .out_8(black_01_64_out_8));
  Black_01 black_01_65 (
    .in_2(black_01_68_out_6), .in_3(black_01_64_out_7), .in_4(black_01_68_out_8), .in_1(black_01_64_out_5),
    .out_5(black_01_65_out_5), .out_6(black_01_65_out_6), .out_7(black_01_65_out_7), .out_8(black_01_65_out_8));
  Maroon_00 maroon_00_27 (
    .in_1(black_01_65_out_5), .in_2(maroon_00_31_out_4), .in_3(black_01_65_out_7), .out_4(maroon_00_27_out_4));
  xor xor_27 (Result[6], grey_01_25_out_6, maroon_00_27_out_4);
  Grey_01 grey_01_27 (
    .in_1(multiplexer_1_out[4]), .in_2(A[4]), .out_3(grey_01_27_out_3), .out_4(grey_01_27_out_4),
    .out_5(grey_01_27_out_5), .out_6(grey_01_27_out_6), .out_7(grey_01_27_out_7));
  Black_01 black_01_66 (
    .in_2(grey_01_28_out_4), .in_3(grey_01_27_out_5), .in_4(grey_01_28_out_7), .in_1(grey_01_27_out_3),
    .out_5(black_01_66_out_5), .out_6(black_01_66_out_6), .out_7(black_01_66_out_7), .out_8(black_01_66_out_8));
  Black_01 black_01_67 (
    .in_2(black_01_70_out_6), .in_3(black_01_66_out_7), .in_4(black_01_70_out_8), .in_1(black_01_66_out_5),
    .out_5(black_01_67_out_5), .out_6(black_01_67_out_6), .out_7(black_01_67_out_7), .out_8(black_01_67_out_8));
  Maroon_00 maroon_00_28 (
    .in_1(black_01_67_out_5), .in_2(maroon_00_32_out_4), .in_3(black_01_67_out_7), .out_4(maroon_00_28_out_4));
  xor xor_28 (Result[5], grey_01_26_out_6, maroon_00_28_out_4);
  xor xor_29 (Result[4], grey_01_27_out_6, maroon_00_29_out_4);
  Grey_01 grey_01_28 (
    .in_1(multiplexer_1_out[3]), .in_2(A[3]), .out_3(grey_01_28_out_3), .out_4(grey_01_28_out_4),
    .out_5(grey_01_28_out_5), .out_6(grey_01_28_out_6), .out_7(grey_01_28_out_7));
  Black_01 black_01_68 (
    .in_2(grey_01_29_out_4), .in_3(grey_01_28_out_5), .in_4(grey_01_29_out_7), .in_1(grey_01_28_out_3),
    .out_5(black_01_68_out_5), .out_6(black_01_68_out_6), .out_7(black_01_68_out_7), .out_8(black_01_68_out_8));
  Black_01 black_01_69 (
    .in_2(black_01_71_out_6), .in_3(black_01_68_out_7), .in_4(black_01_71_out_8), .in_1(black_01_68_out_5),
    .out_5(black_01_69_out_5), .out_6(black_01_69_out_6), .out_7(black_01_69_out_7), .out_8(black_01_69_out_8));
  Maroon_00 maroon_00_29 (
    .in_1(black_01_69_out_5), .in_2(Subtraction), .in_3(black_01_69_out_7), .out_4(maroon_00_29_out_4));
  Grey_01 grey_01_29 (
    .in_1(multiplexer_1_out[2]), .in_2(A[2]), .out_3(grey_01_29_out_3), .out_4(grey_01_29_out_4),
    .out_5(grey_01_29_out_5), .out_6(grey_01_29_out_6), .out_7(grey_01_29_out_7));
  Black_01 black_01_70 (
    .in_2(grey_01_30_out_4), .in_3(grey_01_29_out_5), .in_4(grey_01_30_out_7), .in_1(grey_01_29_out_3),
    .out_5(black_01_70_out_5), .out_6(black_01_70_out_6), .out_7(black_01_70_out_7), .out_8(black_01_70_out_8));
  Maroon_00 maroon_00_30 (
    .in_1(black_01_70_out_5), .in_2(maroon_00_32_out_4), .in_3(black_01_70_out_7), .out_4(maroon_00_30_out_4));
  xor xor_30 (Result[3], grey_01_28_out_6, maroon_00_30_out_4);
  Grey_01 grey_01_30 (
    .in_1(multiplexer_1_out[1]), .in_2(A[1]), .out_3(grey_01_30_out_3), .out_4(grey_01_30_out_4),
    .out_5(grey_01_30_out_5), .out_6(grey_01_30_out_6), .out_7(grey_01_30_out_7));
  Black_01 black_01_71 (
    .in_2(grey_01_31_out_4), .in_3(grey_01_30_out_5), .in_4(grey_01_31_out_7), .in_1(grey_01_30_out_3),
    .out_5(black_01_71_out_5), .out_6(black_01_71_out_6), .out_7(black_01_71_out_7), .out_8(black_01_71_out_8));
  Maroon_00 maroon_00_31 (
    .in_1(black_01_71_out_5), .in_2(Subtraction), .in_3(black_01_71_out_7), .out_4(maroon_00_31_out_4));
  xor xor_31 (Result[2], grey_01_29_out_6, maroon_00_31_out_4);
  Grey_01 grey_01_31 (
    .in_1(multiplexer_1_out[0]), .in_2(A[0]), .out_3(grey_01_31_out_3), .out_4(grey_01_31_out_4),
    .out_5(grey_01_31_out_5), .out_6(grey_01_31_out_6), .out_7(grey_01_31_out_7));
  Maroon_00 maroon_00_32 (
    .in_1(grey_01_31_out_3), .in_2(Subtraction), .in_3(grey_01_31_out_5), .out_4(maroon_00_32_out_4));
  xor xor_32 (Result[1], grey_01_30_out_6, maroon_00_32_out_4);
  xor xor_33 (Result[0], grey_01_31_out_6, Subtraction);
endmodule

module Maroon_00 (
  input  in_1,
  input  in_2,
  input  in_3,
  output out_4
);

  wire and_1_out;

  and and_1 (and_1_out, in_2, in_3);
  or or_1 (out_4, in_1, and_1_out);
endmodule

module Black_01 (
  input  in_1,
  input  in_2,
  input  in_3,
  input  in_4,
  output out_5,
  output out_6,
  output out_7,
  output out_8
);

  wire and_1_out;

  and and_1 (and_1_out, in_2, in_3);
  or or_1 (out_5, in_1, and_1_out);
  and and_2 (out_7, in_3, in_4);

  assign out_6 = out_5;
  assign out_8 = out_7;
endmodule

module Black_02 (
  input  in_1,
  input  in_2,
  input  in_3,
  input  in_4,
  output b,
  output c
);

  wire and_1_out;

  and and_1 (and_1_out, in_2, in_3);
  or or_1 (b, in_1, and_1_out);
  and and_2 (c, in_3, in_4);
endmodule

// HalfAdder
module Grey_01 (
  input  in_1,
  input  in_2,
  output out_3,
  output out_4,
  output out_5,
  output out_6,
  output out_7
);

  and and_1 (out_3, in_1, in_2);
  xor xor_1 (out_5, in_1, in_2);

  assign out_4 = out_3;
  assign out_6 = out_5;
  assign out_7 = out_5;
endmodule

// HalfAdder
module Grey_02 (
  input  in_1,
  input  in_2,
  output out_3,
  output out_4,
  output out_5
);

  and and_1 (out_3, in_1, in_2);
  xor xor_1 (out_4, in_1, in_2);

  assign out_5 = out_4;
endmodule
